# Fritzing sketch plantoid box Sketch (saved by Fritzing 0.9.2b)
circuit board: 4.1cm x 8.70417cm
breadboards: 1

parts:
  R1 = Resistor [tolerance=±5% resistance=10k package=THT]
  J2 = female pin header, 8 pins [form="♀ (female)"]
  J8 = female pin header, 3 pins [form="♀ (female)"]
  C1 = Electrolytic Capacitor [capacitance=470µF package="100 mil [THT, electrolytic]"]
  J9 = female pin header, 8 pins [form="♀ (female)"]
  J10 = female pin header, 8 pins [form="♀ (female)"]
  J11 = female pin header, 8 pins [form="♀ (female)"]
  IC1 = IC, DIP package, 16 pins [chip_label=IC]
  J13 = female pin header, 4 pins [form="♀ (female)"]
  J12 = female pin header, 4 pins [form="♀ (female)"]
  J14 = female pin header, 4 pins [form="♀ (female)"]
  J15 = female pin header, 2 pins [form="♀ (female)"]

nets:
  N1: R1.Pin_0, J8.pin1, C1.-, J11.pin7, IC1.pin6, IC1.pin7, IC1.pin8, J13.pin4, J12.pin4, J14.pin4, J15.pin2
  N2: R1.Pin_1, J10.pin2, IC1.pin3
  N3: J2.pin1, IC1.pin12
  N4: J2.pin2, IC1.pin13
  N5: J2.pin3, IC1.pin14
  N6: J2.pin4, IC1.pin15
  N7: J2.pin5, IC1.pin1
  N8: J2.pin6, IC1.pin2
  N9: J2.pin7, IC1.pin4
  N10: J2.pin8, IC1.pin5
  N11: J8.pin2, J10.pin7
  N12: J8.pin3, C1.+, J9.pin1, J9.pin2, J9.pin3, J9.pin4, J9.pin5, J9.pin6, J9.pin7, J9.pin8, J11.pin8, IC1.pin16, J13.pin1, J12.pin1, J14.pin1, J15.pin1
  N13: J10.pin3, J13.pin2
  N14: J10.pin4, IC1.pin11
  N15: J10.pin5, IC1.pin10
  N16: J10.pin6, IC1.pin9
  N17: J11.pin3, J12.pin3
  N18: J11.pin4, J12.pin2
  N19: J11.pin5, J14.pin3
  N20: J11.pin6, J14.pin2

notes:
  Wemos D1
  CD4051
  ANALOG IN
  10k
  -
  rst
  5v
  led
  dht
  sonar1
  sonar2
  Plantoïd sensor node
  Vin
  +
